# Fritzing sketch Untitled Sketch 2 (saved by Fritzing 0.8.7b)
breadboards: 1

parts:
  U1 = Module 4 Relais 5V [package="Module 4 Relais 5V"]
  PS1 = prefix0000 [part_number=S-350-60]
  WATER_PUMP1 = water pump/motor  # not connected
  YF-S201_Flow_Meter2 = YF-S201 Water Flow Meter
  F1 = Small Fan, based on Fan - Ventilador [package=THT]
  U2 = ESP32-38PinWide [part_number=ESP32-38PinWide]
  부품1 = Breadboard Power Supply Board SMD  # not connected
  U3 = WS2812 RGB LED strip

nets:
  N1: U1.IN1, U2.GPIO25
  N2: U1.IN2, U2.GPIO26
  N3: U1.IN3, U2.GPIO27
  N4: U1.K1-NF, U2.VIN
  N5: U1.K1-NO, YF-S201_Flow_Meter2.VCC
  N6: U1.K2-NO, U3.VCC
  GND: PS1.connector4, YF-S201_Flow_Meter2.GND, F1.GND, U2.GND, U3.GND

notes:
  dcdc converter
  12V plus
  12V minus
  5V plus
  5V minus
  3V plus
  3V minus
  220+
  220-
  220접지
  power adapter
  +
  -

custom parts:
  Module 4 Relais 5V: Module 4 Relais 5V 4x SPD-06VDC-SD-C
  water pump/motor: WATER PUMP BY ARDUBLOCKTR
  YF-S201 Water Flow Meter: The YF-S201 Flow Meter. The input voltage is 5V to 24V (DC).
  Small Fan, based on Fan - Ventilador: Small 2-pin fan, commonly used with single-board computers, 3d-printers, etc. This work is based on a much larger fan, as commonly found in desktop computers
  ESP32-38PinWide: Generic 38-Pin ESP32 with wide format (only access to one side of pins on a breadboard) based on Stephen Lilley's HiLetgo ESP-WROOM-32 ESP32 ESP-32S Development Board.
  WS2812 RGB LED strip: WS2812 strip
